# Fritzing sketch KY-012 active piezo buzzer (saved by Fritzing 0.9.3b)

parts:
  Mod2 = Raspberry Pi 4B
  Part2 = KY-006 Passive Buzzer Module [package="Breakout board"]

nets:
  N1: Mod2.GND, Part2.-
  N2: Mod2.GPIO24, Part2.S

custom parts:
  KY-006 Passive Buzzer Module: Passive Piezoelectric Buzzer Module Keyes KY-006, it can produce a range of sound tones depending on the input frequency.
