# Fritzing sketch KY-020 Tilt switch (saved by Fritzing 0.9.3b)

parts:
  Mod2 = Raspberry Pi 4B
  Part1 = KY-020 Tilt Switch Module [package="Breakout board"]

nets:
  3V3: Mod2.3V3, Part1.Vin
  N1: Mod2.GND, Part1.-
  N2: Mod2.GPIO24, Part1.S

custom parts:
  KY-020 Tilt Switch Module: KY-020 Arduino tilt switch sensor module. Closes the circuit when it is tilted to the side as long as it is moved with enough force and degree of inclination to activate the ball switch inside.
