# Fritzing sketch KY-029 2-COLOR 3MM LED (saved by Fritzing 0.9.3b)

parts:
  Mod1 = KY-029 Dual Color LED Module [package="Breakout board"]
  Mod2 = Raspberry Pi 4B
  R1 = Resistor [tolerance=±5% resistance=150 package=THT]
  R2 = Resistor [tolerance=±5% resistance=150 package=THT]

nets:
  N1: Mod1.G, Mod2.GND
  N2: Mod1.R, R1.Pin_0
  N3: Mod1.-, R2.Pin_0
  N4: Mod2.GPIO23, R2.Pin_1
  N5: Mod2.GPIO24, R1.Pin_1

custom parts:
  KY-029 Dual Color LED Module: KY-029 Dual Color LED Module consist of a common cathode 5mm red/green LED.
