# Fritzing sketch KY-031 KNOCK SENSOR (saved by Fritzing 0.9.3b)

parts:
  Mod2 = Raspberry Pi 4B
  Mod4 = KY-031 Knock Sensor Module [package="Breakout board"]

nets:
  3V3: Mod2.3V3, Mod4.Vin
  N1: Mod2.GND, Mod4.-
  N2: Mod2.GPIO24, Mod4.S

custom parts:
  KY-031 Knock Sensor Module: KY-031 Knock Sensor module. A vibration sensor that sends a signal when a knock/tap is detected.
