# Fritzing sketch KY-034 7 COLOR LED (saved by Fritzing 0.9.3b)

parts:
  Mod2 = Raspberry Pi 4B
  Mod3 = KY-034 Automatic Flashing Color LED [package="Breakout board"]

nets:
  N1: Mod2.GND, Mod3.-
  N2: Mod2.GPIO24, Mod3.S

custom parts:
  KY-034 Automatic Flashing Color LED: KY-034 Automatic Flashiing Color LED. A 7 color LED that flashes through a sequence of colors, creating a multicolored pattern of flashing light.
