# Fritzing sketch pi and bmp280 (saved by Fritzing 0.9.3b)

parts:
  Part1 = Adafruit_BMP280
  Raspberry_Pi_1 = Raspberry Pi 3 [part_number=RPI-3-V1.2]

nets:
  3.3V: Part1.3.3V, Raspberry_Pi_1.3v3
  GND: Part1.GND, Raspberry_Pi_1.GND
  N1: Part1.SCK/SCL, Raspberry_Pi_1.GPIO3
  N2: Part1.SDO/ADR, Raspberry_Pi_1.GPIO2

custom parts:
  Adafruit_BMP280: Bosch has stepped up their game with their new BMP280 sensor, an environmental sensor with temperature, barometric pressure that is the next generation upgrade to the BMP085/BMP180/BMP183. This sensor is great for all sorts of weather sensing and can even be used in both I2C and SPI! This precision sensor from Bosch is the best low-cost, precision sensing solution for measuring barometric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
