# Fritzing sketch pi and cap sensor (saved by Fritzing 0.9.0b)

parts:
  CAPSENSE1 = AT42QT1010 Momentary Capsense Breakout
  RaspberryPi1 = Raspberry Pi Model B

nets:
  GND: CAPSENSE1.GND, RaspberryPi1.GND
  N1: CAPSENSE1.OUT, RaspberryPi1.#23
  VDD: CAPSENSE1.VDD, RaspberryPi1.3V3

custom parts:
  AT42QT1010 Momentary Capsense Breakout: A capacitive touch momentary switch breakout for the AT42QT1010 chip.
  Raspberry Pi Model B: Raspberry Pi (Model B)
