# Fritzing sketch pi and dht12 (saved by Fritzing 0.9.3b)

parts:
  Raspberry_Pi_1 = Raspberry Pi 3 [part_number=RPI-3-V1.2]
  DHT1 = DHT12 Humitidy and Temperature Sensor I2C.

nets:
  N1: Raspberry_Pi_1.GPIO2, DHT1.SDA
  N2: Raspberry_Pi_1.GPIO3, DHT1.SCL
  GND: Raspberry_Pi_1.GND, DHT1.GND
  5V: Raspberry_Pi_1.5V, DHT1.VDD

custom parts:
  DHT12 Humitidy and Temperature Sensor I2C.: DHT12 Humidity and Temperature Sensor I2C. Supply voltage: 2.7V to 5.5V Current: Standby 30uA, Active 800uA Temperature: -20ºC to 60ºC, res. 0.1ºC Humidity: 20%RH to 95%RH, res. 0.1%RH ID I2C 0x5c
