# Fritzing sketch pi and ds18b20 and led (saved by Fritzing 0.9.0b)

parts:
  Raspberry_Pi1 = Raspberry Pi B rev2
  R1 = Resistor [tolerance=±5% resistance=4.7k package=THT]
  DS2 = DS18B20 1-Wire Temperature Sensor [part_number=DS18B20]
  R2 = Resistor [tolerance=±5% resistance=220 package=THT]
  LED1 = LED - 5mm [color="Red (633nm)" package="5 mm [THT]"]

nets:
  3V3: Raspberry_Pi1.3V3, R1.Pin_0, DS2.VDD
  GND: Raspberry_Pi1.GND, DS2.GND, LED1.cathode
  N1: Raspberry_Pi1.GPIO_4, R1.Pin_1, DS2.DQ
  N2: Raspberry_Pi1.GPIO_24, R2.Pin_0
  N3: R2.Pin_1, LED1.anode
