# Fritzing sketch pi and ds18b20 (saved by Fritzing 0.9.0b)

parts:
  Raspberry_Pi1 = Raspberry Pi B rev2
  R1 = Resistor [tolerance=±5% resistance=4.7k package=THT]
  DS2 = DS18B20 1-Wire Temperature Sensor [part_number=DS18B20]

nets:
  3V3: Raspberry_Pi1.3V3, R1.Pin_0, DS2.VDD
  GND: Raspberry_Pi1.GND, DS2.GND
  N1: Raspberry_Pi1.GPIO_4, R1.Pin_1, DS2.DQ
