# Fritzing sketch pi and led (saved by Fritzing 0.9.0b)

parts:
  R1 = Resistor [package="0402 [SMD]"]
  LED1 = smd LED [color="Red (633nm)" package="1206 [SMD]"]
  Raspberry_Pi1 = Raspberry Pi B rev2

nets:
  N1: R1.Pin_0, LED1.anode
  N2: R1.Pin_1, Raspberry_Pi1.GPIO_4
  N3: LED1.cathode, Raspberry_Pi1.GND
